// Logisim project ex5.circ as structural Verilog: 1 circuit, main circuit main
module main (
  input  A,
  input  B,
  output out_3
);

  wire not_1_out;

  not not_1 (not_1_out, B);
  or or_1 (out_3, A, not_1_out);
endmodule
