// Logisim project ex6.circ as structural Verilog: 6 circuits, main circuit RotRight
module RotRight (
  input  [15:0] INPUT0,
  input  [3:0] AMOUNT,
  output [15:0] OUTPUT0
);

  wire [15:0] multiplexer_1_out, multiplexer_2_out, multiplexer_3_out, rotright1_1_out_2, rotright2_1_out_2,
       rotright4_1_out_2, rotright8_1_out_2;

  RotRight1 rotright1_1 (.in_1(INPUT0), .out_2(rotright1_1_out_2));
  Multiplexer #(.enable("false"), .width(16)) multiplexer_1 (
    .in0(INPUT0), .in1(rotright1_1_out_2), .out(multiplexer_1_out), .sel(AMOUNT[0]));
  Multiplexer #(.enable("false"), .width(16)) multiplexer_2 (
    .in0(multiplexer_1_out), .in1(rotright2_1_out_2), .out(multiplexer_2_out), .sel(AMOUNT[1]));
  RotRight2 rotright2_1 (.in_1(multiplexer_1_out), .out_2(rotright2_1_out_2));
  RotRight4 rotright4_1 (.in_1(multiplexer_2_out), .out_2(rotright4_1_out_2));
  Multiplexer #(.enable("false"), .width(16)) multiplexer_3 (
    .in0(multiplexer_2_out), .in1(rotright4_1_out_2), .out(multiplexer_3_out), .sel(AMOUNT[2]));
  Multiplexer #(.enable("false"), .width(16)) multiplexer_4 (
    .in0(multiplexer_3_out), .in1(rotright8_1_out_2), .out(OUTPUT0), .sel(AMOUNT[3]));
  RotRight8 rotright8_1 (.in_1(multiplexer_3_out), .out_2(rotright8_1_out_2));
endmodule

module RotRight1 (
  input  [15:0] in_1,
  output [15:0] out_2
);


  assign out_2 = {in_1[0], in_1[15:1]};
endmodule

module RotRight2 (
  input  [15:0] in_1,
  output [15:0] out_2
);


  assign out_2 = {in_1[1:0], in_1[15:2]};
endmodule

module RotRight4 (
  input  [15:0] in_1,
  output [15:0] out_2
);


  assign out_2 = {in_1[3:0], in_1[15:4]};
endmodule

module RotRight8 (
  input  [15:0] in_1,
  output [15:0] out_2
);


  assign out_2 = {in_1[7:0], in_1[15:8]};
endmodule

module Test (
  output [15:0] out_1
);

  RotRight rotright_1 (.INPUT0(16'h8005), .AMOUNT(4'b1010), .OUTPUT0(out_1));
endmodule
